// Logisim project computer.circ as structural Verilog: 13 circuits, main circuit main
module main (
);

  wire alu_1_c, alu_1_z, C0, C1, C2, C3, C4, C5, C6, C7, C8, C9, C10, C11, C12, C13, C14, C15, C16, C17, C18,
       C19, C20, C21, C22, C23, C24, C25, C26, C27, C28, C29, CLK, comparator_1_eq, flag_1_c_out,
       flag_1_z_out, RESET;
  wire [3:0] output_1_high, output_1_low, \µ_code_step_1_step ;
  wire [6:0] cir_1_op;
  wire [7:0] alu_1_d_out;
  wire [15:0] mar_1_a_out, pc_1_monitor, stack_ptr_1_monitor;
  wire [31:30] decoder_1_c_2;

  Button button_1 (.out(RESET));
  clock clock_1 (.HALT(C19), .CLK(CLK));
  mar mar_1 (
    .CLK(CLK), .A_IN(mar_1_a_out), .D(alu_1_d_out), .A_OUT(mar_1_a_out), .ADDR_IN(C7), .FROM_ADRB(C9),
    .TO_ADRB(C8), .PAGE_IN(C6), .RESET(RESET));
  alu alu_1 (
    .D_IN(alu_1_d_out), .LATCH_ACC(C12), .SUB(C10), .SUM__ACC(C11), .Z(alu_1_z), .ACC_IN(C15), .ACC_OUT(C14),
    .D_OUT(alu_1_d_out), .CLK(CLK), .C(alu_1_c), .RESET(RESET));
  // Probe on mar_1_a_out
  // Probe on alu_1_d_out
  // Probe on pc_1_monitor
  flag flag_1 (
    .Z_IN(alu_1_z), .C_IN(alu_1_c), .LOAD(C13), .Z_OUT(flag_1_z_out), .C_OUT(flag_1_c_out), .CLK(CLK),
    .RESET(RESET));
  Hex_Digit_Display hex_digit_display_1 (.value(mar_1_a_out[11:8]));  // open: dp
  Hex_Digit_Display hex_digit_display_2 (.value(mar_1_a_out[15:12]));  // open: dp
  Hex_Digit_Display hex_digit_display_3 (.value(alu_1_d_out[3:0]));  // open: dp
  Hex_Digit_Display hex_digit_display_4 (.value(alu_1_d_out[7:4]));  // open: dp
  register A (.D_IN(alu_1_d_out), .CLK(CLK), .D_OUT(alu_1_d_out), .IN(C1), .OUT(C0), .RESET(RESET));
  register B (.D_IN(alu_1_d_out), .CLK(CLK), .D_OUT(alu_1_d_out), .IN(C3), .OUT(C2), .RESET(RESET));
  ram ram_1 (.OUT(C4), .D_OUT(alu_1_d_out), .A(mar_1_a_out), .D_IN(alu_1_d_out), .IN(C5));
  pc pc_1 (
    .JUMP(C16), .A_IN(mar_1_a_out), .COUNT(C17), .A_OUT(mar_1_a_out), .CLK(CLK), .OUT(C18),
    .MONITOR(pc_1_monitor), .RESET(RESET), .D_OUT(alu_1_d_out), .ADDR_OUT(C28), .PAGE_OUT(C29));
  cir cir_1 (
    .OP_IN(C20), .D_IN(alu_1_d_out), .D_OUT(alu_1_d_out), .OP(cir_1_op), .CLK(CLK), .ARG_OUT(C21),
    .ARG_IN(C22), .RESET(RESET));
  \µ_code_step  \u_µ_code_step_1  (.CLK(CLK), .STEP(\µ_code_step_1_step ), .RESET(RESET), ._0(comparator_1_eq));
  // Probe on \µ_code_step_1_step 
  Hex_Digit_Display hex_digit_display_5 (.value(mar_1_a_out[3:0]));  // open: dp
  Hex_Digit_Display hex_digit_display_6 (.value(mar_1_a_out[7:4]));  // open: dp
  // Probe on cir_1_op
  stack_ptr stack_ptr_1 (
    .MONITOR(stack_ptr_1_monitor), .SET(C24), .A_IN(mar_1_a_out), .A_OUT(mar_1_a_out), .RESET(RESET),
    .INCR(C25), .OUT(C27), .CLK(CLK), .DECR(C26));
  decoder decoder_1 (
    .STEP(\µ_code_step_1_step ), .C(flag_1_c_out), .Z(flag_1_z_out), .OP(cir_1_op),
    .C_2({decoder_1_c_2, C29, C28, C27, C26, C25, C24, C23, C22, C21, C20, C19, C18, C17, C16, C15, C14, C13, C12, C11, C10, C9, C8, C7, C6, C5, C4, C3, C2, C1, C0}));
  Comparator #(.width(32), .mode("unsigned")) comparator_1 (
    .a({decoder_1_c_2, C29, C28, C27, C26, C25, C24, C23, C22, C21, C20, C19, C18, C17, C16, C15, C14, C13, C12, C11, C10, C9, C8, C7, C6, C5, C4, C3, C2, C1, C0}),
    .b({32{1'b0}}), .eq(comparator_1_eq));  // open: gt, lt
  Hex_Digit_Display hex_digit_display_7 (.value(output_1_high));  // open: dp
  Hex_Digit_Display hex_digit_display_8 (.value(output_1_low));  // open: dp
  \output  output_1 (.D(alu_1_d_out), .IN(C23), .CLK(CLK), .RESET(RESET), .LOW(output_1_low), .HIGH(output_1_high));
  // Probe on stack_ptr_1_monitor

  // Notes on the sheet:
  //   Clock
  //   Memory Address Register
  //   Arithmetic + Logic Unit
  //   Address Bus
  //   Data Bus
  //   A Register
  //   B Register
  //   Memory
  //   Program Counter
  //   Current Instruction
  //   Register
  //   Instruction Decoder
  //   Output
  //   Stack Pointer
  //   Microcode
  //   Resetter
endmodule

// REG
module register (
  input  [7:0] D_IN,
  input  IN,
  input  OUT,
  input  CLK,
  input  RESET,
  output [7:0] D_OUT
);

  wire not_1_out;
  wire [7:0] register_1_q;

  not not_1 (not_1_out, CLK);
  assign D_OUT = OUT ? register_1_q : 8'bz;  // Controlled_Buffer controlled_buffer_1
  Register register_1 (.D(D_IN), .en(IN), .Q(register_1_q), .clk(not_1_out), .clr(RESET));
endmodule

// RAM
module ram (
  input  OUT,
  input  [15:0] A,
  input  [7:0] D_IN,
  input  IN,
  output [7:0] D_OUT
);

  wire or_1_out;
  wire [7:0] ram_1_data;

  or or_1 (or_1_out, OUT, IN);
  RAM #(.addrWidth(16), .bus("asynch")) ram_1 (.addr(A), .data(ram_1_data), .sel(or_1_out), .ld(OUT));  // open: clr
  assign D_OUT = OUT ? ram_1_data : 8'bz;  // Controlled_Buffer controlled_buffer_1
  assign ram_1_data = IN ? D_IN : 8'bz;  // Controlled_Buffer controlled_buffer_2
endmodule

// MAR
module mar (
  input  CLK,
  input  [15:0] A_IN,
  input  [7:0] D,
  input  RESET,
  input  ADDR_IN,
  input  PAGE_IN,
  input  FROM_ADRB,
  input  TO_ADRB,
  output [15:0] A_OUT
);

  wire or_1_out, or_2_out;
  wire [7:0] multiplexer_1_out, multiplexer_2_out;

  Multiplexer #(.width(8), .enable("false")) multiplexer_1 (
    .in0(A_IN[7:0]), .in1(D), .out(multiplexer_1_out), .sel(ADDR_IN));
  register ADDR (.D_IN(multiplexer_1_out), .CLK(CLK), .D_OUT(A_OUT[7:0]), .IN(or_1_out), .OUT(TO_ADRB), .RESET(RESET));
  or or_1 (or_1_out, ADDR_IN, FROM_ADRB);
  register PAGE (.D_IN(multiplexer_2_out), .CLK(CLK), .D_OUT(A_OUT[15:8]), .IN(or_2_out), .OUT(TO_ADRB), .RESET(RESET));
  Multiplexer #(.width(8), .enable("false")) multiplexer_2 (
    .in0(A_IN[15:8]), .in1(D), .out(multiplexer_2_out), .sel(PAGE_IN));
  or or_2 (or_2_out, PAGE_IN, FROM_ADRB);
endmodule

// ALU
module alu (
  input  [7:0] D_IN,
  input  LATCH_ACC,
  input  SUB,
  input  CLK,
  input  SUM__ACC,
  input  RESET,
  input  ACC_IN,
  input  ACC_OUT,
  output C,
  output Z,
  output [7:0] D_OUT
);

  wire nor_1_out, nor_2_out, nor_3_out, nor_4_out, not_1_out, not_2_out, or_1_out;
  wire [7:0] Accumulator_q, adder_1_out, bit_extender_1_out, controlled_buffer_1_out,
       controlled_buffer_2_out, Latch_q, multiplexer_1_out, xor_1_out;

  Multiplexer #(.width(8), .enable("false")) multiplexer_1 (
    .in0(D_IN), .in1(controlled_buffer_1_out), .out(multiplexer_1_out), .sel(SUM__ACC));
  assign controlled_buffer_1_out = SUM__ACC ? adder_1_out : 8'bz;  // Controlled_Buffer controlled_buffer_1
  or or_1 (or_1_out, SUM__ACC, ACC_IN);
  Register Accumulator (.D(multiplexer_1_out), .en(or_1_out), .Q(Accumulator_q), .clk(not_1_out), .clr(RESET));
  not not_1 (not_1_out, CLK);
  assign controlled_buffer_2_out = LATCH_ACC ? Accumulator_q : 8'bz;  // Controlled_Buffer controlled_buffer_2
  not not_2 (not_2_out, CLK);
  assign D_OUT = ACC_OUT ? Accumulator_q : 8'bz;  // Controlled_Buffer controlled_buffer_3
  Register Latch (.D(controlled_buffer_2_out), .en(LATCH_ACC), .Q(Latch_q), .clk(not_2_out), .clr(RESET));
  and and_1 (Z, nor_1_out, nor_2_out, nor_3_out, nor_4_out);
  assign bit_extender_1_out = {{7{SUB}}, SUB};  // Bit_Extender bit_extender_1
  nor nor_1 (nor_1_out, adder_1_out[0], adder_1_out[1]);
  nor nor_2 (nor_2_out, adder_1_out[2], adder_1_out[3]);
  nor nor_3 (nor_3_out, adder_1_out[4], adder_1_out[5]);
  nor nor_4 (nor_4_out, adder_1_out[6], adder_1_out[7]);
  assign xor_1_out = bit_extender_1_out ^ D_IN;  // XOR_Gate xor_1, 8 bits wide
  Adder adder_1 (.a(Latch_q), .b(xor_1_out), .out(adder_1_out), .cin(SUB), .cout(C));
  // Probe on adder_1_out
endmodule

// FLAG
module flag (
  input  Z_IN,
  input  C_IN,
  input  LOAD,
  input  CLK,
  input  RESET,
  output Z_OUT,
  output C_OUT
);

  wire not_1_out;

  Register #(.width(2)) register_1 (.D({C_IN, Z_IN}), .en(LOAD), .Q({C_OUT, Z_OUT}), .clk(not_1_out), .clr(RESET));
  not not_1 (not_1_out, CLK);
endmodule

// CLOCK
module clock (
  input  HALT,
  output CLK
);

  wire clock_1_out, not_1_out;

  Clock clock_1 (.out(clock_1_out));
  and and_1 (CLK, clock_1_out, not_1_out);
  not not_1 (not_1_out, HALT);
endmodule

// PC
module pc (
  input  ADDR_OUT,
  input  PAGE_OUT,
  input  JUMP,
  input  [15:0] A_IN,
  input  RESET,
  input  COUNT,
  input  OUT,
  input  CLK,
  output [7:0] D_OUT,
  output [15:0] MONITOR,
  output [15:0] A_OUT
);

  wire or_1_out, xor_1_out;

  Counter #(.width(16), .max('hffff)) counter_1 (
    .load(JUMP), .D(A_IN), .count(COUNT), .Q(MONITOR), .clk(xor_1_out), .clr(RESET));  // open: carry
  xor xor_1 (xor_1_out, JUMP, CLK);
  or or_1 (or_1_out, ADDR_OUT, PAGE_OUT);
  assign A_OUT = OUT ? MONITOR : 16'bz;  // Controlled_Buffer controlled_buffer_1
  Multiplexer #(.width(8)) multiplexer_1 (
    .in0(MONITOR[7:0]), .in1(MONITOR[15:8]), .out(D_OUT), .sel(PAGE_OUT), .en(or_1_out));
endmodule

// CIR
module cir (
  input  OP_IN,
  input  [7:0] D_IN,
  input  RESET,
  input  CLK,
  input  ARG_OUT,
  input  ARG_IN,
  output [6:0] OP,
  output [7:0] D_OUT
);

  wire [7:7] register_1_q;

  Register register_1 (.D(D_IN), .en(OP_IN), .Q({register_1_q[7], OP}), .clk(CLK), .clr(RESET));
  register ARG (.D_IN(D_IN), .CLK(CLK), .D_OUT(D_OUT), .IN(ARG_IN), .OUT(ARG_OUT), .RESET(RESET));
endmodule

// DEC
module decoder (
  input  [3:0] STEP,
  input  C,
  input  Z,
  input  [6:0] OP,
  output [31:0] C_2
);

  ROM #(.addrWidth(13), .dataWidth(32)) rom_1 (.addr({OP, Z, C, STEP}), .data(C_2));  // open: sel

  // Notes on the sheet:
  //   contents of rom_1 (hex, n*v repeats v):
  //   140010 20000 440010 20000 80000 11*0 140010 20000 440010 20000 80000 11*0 140010 20000 440010 20000
  //   80000 11*0 140010 20000 440010 20000 80000 11*0 140010 20000 440010 20000 200080 8110 10*0 140010
  //   20000 440010 20000 200080 8110 10*0 140010 20000 440010 20000 200080 8110 10*0 140010 20000 440010
  //   20000 200080 8110 10*0 140010 20000 440010 20000 200080 4120 10*0 140010 20000 440010 20000 200080
  //   4120 10*0 140010 20000 440010 20000 200080 4120 10*0 140010 20000 440010 20000 200080 4120 10*0
  //   140010 20000 440010 20000 804000 11*0 140010 20000 440010 20000 804000 11*0 140010 20000 440010
  //   20000 804000 11*0 140010 20000 440010 20000 804000 11*0 140010 20000 440010 20000 12*0 140010 20000
  //   440010 20000 12*0 140010 20000 440010 20000 12*0 140010 20000 440010 20000 12*0 140010 20000 440010
  //   20000 200080 190 8110 9*0 140010 20000 440010 20000 200080 190 8110 9*0 140010 20000 440010 20000
  //   200080 190 8110 9*0 140010 20000 440010 20000 200080 190 8110 9*0 140010 20000 440010 20000 9 11*0
  //   140010 20000 440010 20000 9 11*0 140010 20000 440010 20000 9 11*0 140010 20000 440010 20000 9 11*0
  //   140010 20000 440010 20000 8001 11*0 140010 20000 440010 20000 8001 11*0 140010 20000 440010 20000
  //   8001 11*0 140010 20000 440010 20000 8001 11*0 140010 20000 440010 20000 81 8110 10*0 140010 20000
  //   440010 20000 81 8110 10*0 140010 20000 440010 20000 81 8110 10*0 140010 20000 440010 20000 81 8110
  //   10*0 140010 20000 440010 20000 6 11*0 140010 20000 440010 20000 6 11*0 140010 20000 440010 20000 6
  //   11*0 140010 20000 440010 20000 6 11*0 140010 20000 440010 20000 84 8110 10*0 140010 20000 440010
  //   20000 84 8110 10*0 140010 20000 440010 20000 84 8110 10*0 140010 20000 440010 20000 84 8110 10*0
  //   140010 20000 440010 20000 8004 11*0 140010 20000 440010 20000 8004 11*0 140010 20000 440010 20000
  //   8004 11*0 140010 20000 440010 20000 8004 11*0 140010 20000 440010 20000 200080 190 4120 9*0 140010
  //   20000 440010 20000 200080 190 4120 9*0 140010 20000 440010 20000 200080 190 4120 9*0 140010 20000
  //   440010 20000 200080 190 4120 9*0 140010 20000 440010 20000 4002 11*0 140010 20000 440010 20000 4002
  //   11*0 140010 20000 440010 20000 4002 11*0 140010 20000 440010 20000 4002 11*0 140010 20000 440010
  //   20000 4008 11*0 140010 20000 440010 20000 4008 11*0 140010 20000 440010 20000 4008 11*0 140010 20000
  //   440010 20000 4008 11*0 140010 20000 440010 20000 81 4120 10*0 140010 20000 440010 20000 81 4120 10*0
  //   140010 20000 440010 20000 81 4120 10*0 140010 20000 440010 20000 81 4120 10*0 140010 20000 440010
  //   20000 201080 2910 10*0 140010 20000 440010 20000 201080 2910 10*0 140010 20000 440010 20000 201080
  //   2910 10*0 140010 20000 440010 20000 201080 2910 10*0 140010 20000 440010 20000 1000 2801 10*0 140010
  //   20000 440010 20000 1000 2801 10*0 140010 20000 440010 20000 1000 2801 10*0 140010 20000 440010 20000
  //   1000 2801 10*0 140010 20000 440010 20000 1000 2804 10*0 140010 20000 440010 20000 1000 2804 10*0
  //   140010 20000 440010 20000 1000 2804 10*0 140010 20000 440010 20000 1000 2804 10*0 140010 20000
  //   440010 20000 84 4120 10*0 140010 20000 440010 20000 84 4120 10*0 140010 20000 440010 20000 84 4120
  //   10*0 140010 20000 440010 20000 84 4120 10*0 140010 20000 440010 20000 201080 2d10 10*0 140010 20000
  //   440010 20000 201080 2d10 10*0 140010 20000 440010 20000 201080 2d10 10*0 140010 20000 440010 20000
  //   201080 2d10 10*0 140010 20000 440010 20000 1000 2c01 10*0 140010 20000 440010 20000 1000 2c01 10*0
  //   140010 20000 440010 20000 1000 2c01 10*0 140010 20000 440010 20000 1000 2c01 10*0 140010 20000
  //   440010 20000 1000 2c04 10*0 140010 20000 440010 20000 1000 2c04 10*0 140010 20000 440010 20000 1000
  //   2c04 10*0 140010 20000 440010 20000 1000 2c04 10*0 140010 20000 440010 20000 200040 11*0 140010
  //   20000 440010 20000 200040 11*0 140010 20000 440010 20000 200040 11*0 140010 20000 440010 20000
  //   200040 11*0 140010 20000 440010 20000 200080 10100 10*0 140010 20000 440010 20000 200080 10100 10*0
  //   140010 20000 440010 20000 200080 10100 10*0 140010 20000 440010 20000 200080 10100 10*0 140010 20000
  //   440010 20000 12*0 140010 20000 440010 20000 12*0 140010 200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
endmodule

// STP
module \µ_code_step  (
  input  CLK,
  input  RESET,
  input  _0,
  output [3:0] STEP
);

  wire and_1_out, d_ff_1_q, not_1_out, or_1_out;

  not not_1 (not_1_out, CLK);
  D_Flip_Flop d_ff_1 (.clk(not_1_out), .D(1'b1), .Q(d_ff_1_q), .reset(RESET));  // open: Qn, preset, en
  and and_1 (and_1_out, d_ff_1_q, CLK);
  or or_1 (or_1_out, RESET, _0);
  Counter #(.width(4), .max('hf)) counter_1 (
    .count(1'b1), .Q(STEP), .clk(and_1_out), .clr(or_1_out));  // open: load, D, carry
endmodule

// OUT
module \output  (
  input  [7:0] D,
  input  IN,
  input  CLK,
  input  RESET,
  output [3:0] LOW,
  output [3:0] HIGH
);

  wire not_1_out;

  Register register_1 (.D(D), .en(IN), .Q({HIGH, LOW}), .clk(not_1_out), .clr(RESET));
  not not_1 (not_1_out, CLK);
endmodule

// STACK PTR
module stack_ptr (
  input  SET,
  input  [15:0] A_IN,
  input  RESET,
  input  INCR,
  input  DECR,
  input  OUT,
  input  CLK,
  output [15:0] MONITOR,
  output [15:0] A_OUT
);

  wire or_1_out, or_2_out, xor_1_out;

  or or_1 (or_1_out, SET, DECR);
  or or_2 (or_2_out, INCR, DECR);
  Counter #(.width(16), .max('hffff)) counter_1 (
    .load(or_1_out), .D(A_IN), .count(or_2_out), .Q(MONITOR), .clk(xor_1_out), .clr(RESET));  // open: carry
  xor xor_1 (xor_1_out, SET, CLK);
  assign A_OUT = OUT ? MONITOR : 16'bz;  // Controlled_Buffer controlled_buffer_1
endmodule
